# Fritzing sketch schematic (saved by Fritzing 0.9.4)
breadboards: 1

parts:
  Arduino_Nano_Every = Arduino Nano (Rev3.0)
  Adafruit_MCP4725_breakout = Adafruit MCP4725 Breakout Board - 12-Bit DAC [part_number="Adafruit #935"]
  DS1 = DS18B20 1-Wire Temperature Sensor [part_number=DS18B20]
  Thermostat = Header 3 [package=screwterminal-3.5mm-3_lock.007s]

nets:
  GND: Arduino_Nano_Every.GND, DS1.GND, Thermostat.2
  N1: Arduino_Nano_Every.D2, Arduino_Nano_Every.D3, DS1.DQ
  N2: Arduino_Nano_Every.D4, DS1.VDD
  N3: Arduino_Nano_Every.5V, Thermostat.3
  N4: Arduino_Nano_Every.A7, Adafruit_MCP4725_breakout.VDD
  N5: Arduino_Nano_Every.A6, Adafruit_MCP4725_breakout.GND
  N6: Arduino_Nano_Every.A5, Adafruit_MCP4725_breakout.SCL
  N7: Arduino_Nano_Every.A4, Adafruit_MCP4725_breakout.SDA
  N8: Arduino_Nano_Every.A3, Adafruit_MCP4725_breakout.A0
  N9: Arduino_Nano_Every.A2, Adafruit_MCP4725_breakout.VOUT, Thermostat.1

custom parts:
  Adafruit MCP4725 Breakout Board - 12-Bit DAC: Your microcontroller probably has an ADC (analog -> digital converter) but does it have a DAC (digital -> analog converter)??? Now it can! This breakout board features the easy-to-use MCP4725 12-bit DAC. Control it via I2C and send it the value you want it to output, and the VOUT pin will have it. Great for audio / analog projects, such as when you can't use PWM but need a sine wave or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
